// Logisim project dinozaur wyswietlanie.circ as structural Verilog: 1 circuit, main circuit main
module main (
  input  guzik_1,
  input  clock,
  input  stop,
  output [31:0] dino15,
  output [31:0] dino14,
  output [31:0] dino13,
  output [31:0] dino12,
  output [31:0] dino11,
  output [31:0] dino10,
  output [31:0] dino9,
  output [31:0] dino8,
  output [31:0] dino7,
  output [31:0] dino6,
  output [31:0] dino5,
  output [31:0] dino4,
  output [31:0] dino3,
  output [31:0] dino2,
  output [31:0] dino1,
  output [31:0] dino0
);

  wire and_1_out, and_2_out, and_3_out, and_4_out, and_5_out, and_6_out, and_7_out, and_8_out, and_9_out,
       and_10_out, and_11_out, and_12_out, and_13_out, and_14_out, and_15_out, and_16_out, and_17_out,
       and_18_out, and_19_out, and_20_out, and_21_out, and_22_out, and_23_out, and_24_out, and_25_out,
       and_26_out, and_27_out, not_1_out, or_1_out, or_2_out, or_3_out, or_4_out, or_5_out, or_6_out,
       or_7_out, or_8_out, or_9_out, or_10_out, or_11_out;
  wire [2:0] counter_2_q;
  wire [3:0] counter_1_q;
  wire [31:0] controlled_buffer_1_out;

  and and_1 (and_1_out, counter_1_q[3], counter_1_q[2], counter_1_q[0], ~counter_1_q[1]);  // AND_Gate
  or or_1 (or_1_out, and_1_out, and_2_out);
  and and_2 (and_2_out, ~counter_1_q[1], ~counter_1_q[0], ~counter_1_q[2], ~counter_1_q[3]);  // AND_Gate
  or or_2 (or_2_out, and_3_out, and_7_out);
  and and_3 (and_3_out, ~counter_2_q[2], ~counter_2_q[1], counter_2_q[0]);  // AND_Gate
  and and_4 (and_4_out, counter_1_q[0], counter_1_q[1], counter_1_q[2], ~counter_1_q[3]);  // AND_Gate
  or or_3 (or_3_out, and_5_out, and_10_out);
  and and_5 (and_5_out, ~counter_1_q[1], ~counter_1_q[2], counter_1_q[0], ~counter_1_q[3]);  // AND_Gate
  and and_6 (and_6_out, clock, guzik_1);
  and and_7 (and_7_out, ~counter_2_q[0], counter_2_q[1], ~counter_2_q[2]);  // AND_Gate
  and and_8 (and_8_out, counter_1_q[3], ~counter_1_q[2], ~counter_1_q[1], ~counter_1_q[0]);  // AND_Gate
  and and_9 (and_9_out, counter_1_q[3], ~counter_1_q[2], counter_1_q[0], ~counter_1_q[1]);  // AND_Gate
  and and_10 (and_10_out, counter_1_q[3], counter_1_q[2], ~counter_1_q[1], ~counter_1_q[0]);  // AND_Gate
  Counter #(.width(4), .max('hf)) counter_1 (
    .Q(counter_1_q), .clk(or_4_out), .clr(or_5_out));  // open: load, D, count, carry
  or or_4 (or_4_out, and_6_out, and_11_out);
  and and_11 (and_11_out, clock, not_1_out);
  assign controlled_buffer_1_out = or_2_out ? 32'h8000000 : 32'bz;  // Controlled_Buffer controlled_buffer_1
  and and_12 (and_12_out, counter_1_q[1], ~counter_1_q[0], counter_1_q[3], ~counter_1_q[2]);  // AND_Gate
  and and_13 (and_13_out, and_26_out, ~guzik_1);  // AND_Gate
  or or_5 (or_5_out, and_13_out, and_18_out, stop);
  not not_1 (not_1_out, and_26_out);
  or or_6 (or_6_out, or_8_out, or_3_out);
  assign controlled_buffer_1_out = or_7_out ? 32'h20000000 : 32'bz;  // Controlled_Buffer controlled_buffer_2
  or or_7 (or_7_out, and_14_out, and_20_out);
  and and_14 (and_14_out, ~counter_2_q[0], counter_2_q[1], counter_2_q[2]);  // AND_Gate
  Counter #(.width(3), .max('h7)) counter_2 (.Q(counter_2_q), .clk(clock), .clr(stop));  // open: load, D, count, carry
  and and_15 (and_15_out, counter_1_q[0], ~counter_1_q[2], counter_1_q[1], counter_1_q[3]);  // AND_Gate
  and and_16 (and_16_out, counter_1_q[0], counter_1_q[1], ~counter_1_q[2], ~counter_1_q[3]);  // AND_Gate
  and and_17 (and_17_out, ~counter_1_q[0], ~counter_1_q[2], counter_1_q[1], ~counter_1_q[3]);  // AND_Gate
  and and_18 (and_18_out, counter_1_q[3], ~counter_1_q[1], counter_1_q[0], counter_1_q[2]);  // AND_Gate
  assign controlled_buffer_1_out = or_9_out ? 32'h28000000 : 32'bz;  // Controlled_Buffer controlled_buffer_3
  and and_19 (and_19_out, counter_2_q[2], counter_2_q[0], counter_2_q[1]);
  and and_20 (and_20_out, ~counter_2_q[1], counter_2_q[0], counter_2_q[2]);  // AND_Gate
  or or_8 (or_8_out, and_8_out, and_12_out, and_4_out, and_9_out, and_17_out, and_25_out, and_24_out, and_21_out, and_16_out, and_15_out);
  and and_21 (and_21_out, ~counter_1_q[3], ~counter_1_q[1], ~counter_1_q[0], counter_1_q[2]);  // AND_Gate
  or or_9 (or_9_out, and_19_out, and_22_out, and_27_out, and_23_out);
  and and_22 (and_22_out, ~counter_2_q[0], ~counter_2_q[1], counter_2_q[2]);  // AND_Gate
  and and_23 (and_23_out, ~counter_2_q[2], counter_2_q[0], counter_2_q[1]);  // AND_Gate
  and and_24 (and_24_out, counter_1_q[1], counter_1_q[2], ~counter_1_q[0], ~counter_1_q[3]);  // AND_Gate
  and and_25 (and_25_out, counter_1_q[0], counter_1_q[2], ~counter_1_q[1], ~counter_1_q[3]);  // AND_Gate
  and and_26 (and_26_out, ~counter_1_q[3], ~counter_1_q[2], ~counter_1_q[1], ~counter_1_q[0]);  // AND_Gate
  and and_27 (and_27_out, ~counter_2_q[0], ~counter_2_q[2], ~counter_2_q[1]);  // AND_Gate
  or or_10 (or_10_out, or_3_out, or_1_out);
  assign dino14 = or_10_out ? {32{1'b0}} : 32'bz;  // Controlled_Buffer controlled_buffer_4
  assign dino13 = or_10_out ? {32{1'b0}} : 32'bz;  // Controlled_Buffer controlled_buffer_5
  assign dino12 = or_10_out ? {32{1'b0}} : 32'bz;  // Controlled_Buffer controlled_buffer_6
  assign dino11 = or_10_out ? {32{1'b0}} : 32'bz;  // Controlled_Buffer controlled_buffer_7
  assign dino10 = or_1_out ? {32{1'b0}} : 32'bz;  // Controlled_Buffer controlled_buffer_8
  assign dino9 = or_1_out ? {32{1'b0}} : 32'bz;  // Controlled_Buffer controlled_buffer_9
  assign dino8 = or_11_out ? {32{1'b0}} : 32'bz;  // Controlled_Buffer controlled_buffer_10
  assign dino7 = or_11_out ? {32{1'b0}} : 32'bz;  // Controlled_Buffer controlled_buffer_11
  or or_11 (or_11_out, or_1_out, or_8_out);
  assign dino14 = or_8_out ? 32'h1c000000 : 32'bz;  // Controlled_Buffer controlled_buffer_12
  assign dino13 = or_8_out ? 32'h14000000 : 32'bz;  // Controlled_Buffer controlled_buffer_13
  assign dino12 = or_8_out ? 32'h18000000 : 32'bz;  // Controlled_Buffer controlled_buffer_14
  assign dino10 = or_3_out ? 32'h1c000000 : 32'bz;  // Controlled_Buffer controlled_buffer_15
  assign dino9 = or_3_out ? 32'h14000000 : 32'bz;  // Controlled_Buffer controlled_buffer_16
  assign dino8 = or_3_out ? 32'h18000000 : 32'bz;  // Controlled_Buffer controlled_buffer_17
  assign dino7 = or_3_out ? 32'hbc000000 : 32'bz;  // Controlled_Buffer controlled_buffer_18
  assign dino5 = or_8_out ? {32{1'b0}} : 32'bz;  // Controlled_Buffer controlled_buffer_19
  assign dino11 = or_8_out ? 32'hbc000000 : 32'bz;  // Controlled_Buffer controlled_buffer_20
  assign dino5 = or_3_out ? 32'h28000000 : 32'bz;  // Controlled_Buffer controlled_buffer_21
  assign dino4 = or_6_out ? {32{1'b0}} : 32'bz;  // Controlled_Buffer controlled_buffer_22
  assign dino3 = or_6_out ? {32{1'b0}} : 32'bz;  // Controlled_Buffer controlled_buffer_23
  assign dino3 = or_1_out ? 32'hbc000000 : 32'bz;  // Controlled_Buffer controlled_buffer_24
  assign dino2 = or_6_out ? {32{1'b0}} : 32'bz;  // Controlled_Buffer controlled_buffer_25
  assign dino2 = or_1_out ? 32'h78000000 : 32'bz;  // Controlled_Buffer controlled_buffer_26
  assign dino1 = or_6_out ? {32{1'b0}} : 32'bz;  // Controlled_Buffer controlled_buffer_27
  assign dino10 = or_8_out ? 32'h78000000 : 32'bz;  // Controlled_Buffer controlled_buffer_28
  assign dino6 = or_8_out ? {32{1'b0}} : 32'bz;  // Controlled_Buffer controlled_buffer_29
  assign dino6 = or_3_out ? 32'h78000000 : 32'bz;  // Controlled_Buffer controlled_buffer_30
  assign dino6 = or_1_out ? 32'h1c000000 : 32'bz;  // Controlled_Buffer controlled_buffer_31
  assign dino5 = or_1_out ? 32'h14000000 : 32'bz;  // Controlled_Buffer controlled_buffer_32
  assign dino4 = or_1_out ? 32'h18000000 : 32'bz;  // Controlled_Buffer controlled_buffer_33
  assign dino1 = or_1_out ? controlled_buffer_1_out : 32'bz;  // Controlled_Buffer controlled_buffer_34
  assign dino9 = or_8_out ? 32'h28000000 : 32'bz;  // Controlled_Buffer controlled_buffer_35

  assign dino0 = {32{1'b1}};
  assign dino15 = {32{1'b0}};
endmodule
