// Logisim project kaktus wyswietlanie.circ as structural Verilog: 1 circuit, main circuit main
module main (
  input  [31:0] kaktus_0_klatka,
  input  [31:0] kaktus_1_klatka,
  input  [31:0] kaktus_2_klatka,
  input  [31:0] kaktus_3_klatka,
  input  [31:0] kaktus_4klatka,
  input  [31:0] kaktus_5_klatka,
  input  clock,
  input  stop,
  output [31:0] kaktus_out,
  output clock_out
);

  wire and_1_out, and_2_out, and_4_out, and_5_out, and_6_out, and_7_out, and_8_out, and_9_out, and_10_out,
       and_11_out, and_12_out, and_13_out, and_14_out, and_15_out, and_16_out, or_1_out, or_2_out, or_3_out;
  wire [5:0] counter_1_q;

  and and_1 (and_1_out, stop, clock);
  or or_1 (or_1_out, and_2_out, and_5_out);
  and and_2 (and_2_out, ~counter_1_q[1], ~counter_1_q[3], ~counter_1_q[2], ~counter_1_q[4], ~counter_1_q[0], ~counter_1_q[5]);  // AND_Gate
  // AND_Gate and_3 has open pins: in0=counter_1_q[0], in1=counter_1_q[1], in2=counter_1_q[2], in3=counter_1_q[3], out=open
  and and_4 (and_4_out, clock, ~stop);  // AND_Gate
  assign kaktus_out = or_1_out ? kaktus_0_klatka : 32'bz;  // Controlled_Buffer controlled_buffer_1
  and and_5 (and_5_out, ~counter_1_q[1], ~counter_1_q[3], ~counter_1_q[2], ~counter_1_q[4], counter_1_q[0], ~counter_1_q[5]);  // AND_Gate
  assign kaktus_out = and_6_out ? kaktus_1_klatka : 32'bz;  // Controlled_Buffer controlled_buffer_2
  and and_6 (and_6_out, ~counter_1_q[0], ~counter_1_q[3], ~counter_1_q[2], ~counter_1_q[4], counter_1_q[1], ~counter_1_q[5]);  // AND_Gate
  and and_7 (and_7_out, counter_1_q[5], counter_1_q[2], counter_1_q[1]);
  assign kaktus_out = and_8_out ? kaktus_2_klatka : 32'bz;  // Controlled_Buffer controlled_buffer_3
  and and_8 (and_8_out, ~counter_1_q[5], ~counter_1_q[3], ~counter_1_q[2], counter_1_q[1], counter_1_q[0], ~counter_1_q[4]);  // AND_Gate
  Counter #(.width(6), .max('h3f)) counter_1 (
    .Q(counter_1_q), .clk(and_4_out), .clr(or_2_out));  // open: load, D, count, carry
  or or_2 (or_2_out, and_7_out, and_1_out);
  assign kaktus_out = and_9_out ? kaktus_3_klatka : 32'bz;  // Controlled_Buffer controlled_buffer_4
  and and_9 (and_9_out, ~counter_1_q[1], ~counter_1_q[3], ~counter_1_q[0], ~counter_1_q[4], ~counter_1_q[5], counter_1_q[2]);  // AND_Gate
  assign kaktus_out = and_10_out ? kaktus_4klatka : 32'bz;  // Controlled_Buffer controlled_buffer_5
  and and_10 (and_10_out, ~counter_1_q[4], ~counter_1_q[3], ~counter_1_q[1], counter_1_q[2], counter_1_q[0], ~counter_1_q[5]);  // AND_Gate
  assign kaktus_out = or_3_out ? kaktus_5_klatka : 32'bz;  // Controlled_Buffer controlled_buffer_6
  or or_3 (or_3_out, counter_1_q[4], and_12_out, counter_1_q[5], counter_1_q[3], and_11_out);
  and and_11 (and_11_out, counter_1_q[1], counter_1_q[0], counter_1_q[2]);
  and and_12 (and_12_out, counter_1_q[1], counter_1_q[2]);
  and and_13 (and_13_out, counter_1_q[5], and_4_out);
  or or_4 (clock_out, and_13_out, and_14_out, and_16_out, and_15_out);
  and and_14 (and_14_out, and_11_out, and_4_out);
  and and_15 (and_15_out, and_4_out, counter_1_q[3]);
  and and_16 (and_16_out, counter_1_q[4], and_4_out);
endmodule
