// Logisim project proba2.circ as structural Verilog: 1 circuit, main circuit main
module main (
);

  wire _32_out, _64_out, _128_out, _256_out, comparator_1_eq, comparator_2_eq, controlled_buffer_1_out,
       keyboard_1_avail, main_1_out, \main_2_maly_duży , main_3_out_17, main_4_ptak, main_5__100,
       main_5__1000, main_5__10000, or_1_out, or_2_out, \reset_lub_wciśnij_klawisz_r_out ,
       \skok_lub_wciśnij_spacje_out ;
  wire [6:0] keyboard_1_data;
  wire [15:0] main_5_out_4, main_5_out_5, main_5_out_6, main_5_out_7, main_5_out_8, main_5_out_9,
       main_5_out_10, main_5_out_11, main_5_out_12, main_5_out_13, main_5_out_14, main_5_out_15,
       main_5_out_16, main_5_out_17, main_5_out_18, main_5_out_19, main_5_out_20, main_5_out_21,
       main_5_out_22, main_5_out_23, main_5_out_24, main_5_out_25, main_5_out_26, main_5_out_27,
       main_5_out_28, main_5_out_29, main_5_out_30, main_5_out_31, main_5_out_32, main_5_out_33,
       main_5_out_34, main_5_out_35;
  wire [31:0] main_4_kolizja_wiersz_1, main_4_kolizja_wiersz_2, main_4_kolizja_wiersz_3,
       main_4_kolizja_wiersz_4, main_4_kolizja_wiersz_5, main_4_kolizja_wiersz_6, main_4_kolizja_wiersz_7,
       main_4_kolizja_wiersz_8, main_4_kolizja_wiersz_9, main_4_kolizja_wiersz_10, main_4_kolizja_wiersz_11,
       main_4_kolizja_wiersz_12, main_4_kolizja_wiersz_13, main_4_kolizja_wiersz_14,
       main_4_kolizja_wiersz_15, main_4_out_20, main_4_out_21, main_4_out_22, main_4_out_23, main_4_out_24,
       main_4_out_25, main_4_out_26, main_4_out_27, main_4_out_28, main_4_out_29, main_4_out_30,
       main_4_out_31, main_4_out_32, main_4_out_33, main_4_out_34, main_4_out_35;

  Clock #(.highDuration(8), .lowDuration(8)) _32 (.out(_32_out));
  Clock #(.highDuration(4), .lowDuration(4)) _64 (.out(_64_out));
  Clock #(.highDuration(2), .lowDuration(2)) _128 (.out(_128_out));
  Clock _256 (.out(_256_out));
  clock_zmiana_main main_1 (
    .clock32(_32_out), .clock64(_64_out), .clock128(_128_out), .clock256(_256_out), ._100(main_5__100),
    ._1000(main_5__1000), ._10000(main_5__10000), .out(main_1_out));
  \mały_lub_duży_main  main_2 (
    .clock(main_1_out), .in_2(main_3_out_17), .ptak(main_4_ptak), .\maly_duży (\main_2_maly_duży ));
  assign controlled_buffer_1_out = keyboard_1_avail ? main_1_out : 1'bz;  // Controlled_Buffer controlled_buffer_1
  Keyboard keyboard_1 (
    .clk(controlled_buffer_1_out), .avail(keyboard_1_avail), .data(keyboard_1_data));  // open: re, clr
  przegrana_main main_3 (
    .reset(or_2_out), .out_17(main_3_out_17), .in_4(main_4_kolizja_wiersz_1), .in_5(main_4_kolizja_wiersz_2),
    .in_6(main_4_kolizja_wiersz_3), .in_7(main_4_kolizja_wiersz_4), .in_8(main_4_kolizja_wiersz_5),
    .in_9(main_4_kolizja_wiersz_6), .in_10(main_4_kolizja_wiersz_7), .in_11(main_4_kolizja_wiersz_8),
    .in_12(main_4_kolizja_wiersz_9), .in_13(main_4_kolizja_wiersz_10), .in_14(main_4_kolizja_wiersz_11),
    .in_15(main_4_kolizja_wiersz_12), .in_16(main_4_kolizja_wiersz_13), .in_2(main_4_kolizja_wiersz_14),
    .in_3(main_4_kolizja_wiersz_15));
  DotMatrix #(.matrixcols(32), .matrixrows(16)) dotmatrix_1 (
    .col0(main_5_out_4), .col1(main_5_out_5), .col2(main_5_out_6), .col3(main_5_out_7), .col4(main_5_out_8),
    .col5(main_5_out_9), .col6(main_5_out_10), .col7(main_5_out_11), .col8(main_5_out_12),
    .col9(main_5_out_13), .col10(main_5_out_14), .col11(main_5_out_15), .col12(main_5_out_16),
    .col13(main_5_out_17), .col14(main_5_out_18), .col15(main_5_out_19), .col16(main_5_out_20),
    .col17(main_5_out_21), .col18(main_5_out_22), .col19(main_5_out_23), .col20(main_5_out_24),
    .col21(main_5_out_25), .col22(main_5_out_26), .col23(main_5_out_27), .col24(main_5_out_28),
    .col25(main_5_out_29), .col26(main_5_out_30), .col27(main_5_out_31), .col28(main_5_out_32),
    .col29(main_5_out_33), .col30(main_5_out_34), .col31(main_5_out_35));
  skroceniev2_led_main main_4 (
    .guzik2(or_1_out), .stop(main_3_out_17), .clock(main_1_out), .guzior(\main_2_maly_duży ),
    .ptak(main_4_ptak), .kolizja_wiersz_1(main_4_kolizja_wiersz_1),
    .kolizja_wiersz_2(main_4_kolizja_wiersz_2), .kolizja_wiersz_3(main_4_kolizja_wiersz_3),
    .kolizja_wiersz_4(main_4_kolizja_wiersz_4), .kolizja_wiersz_5(main_4_kolizja_wiersz_5),
    .kolizja_wiersz_6(main_4_kolizja_wiersz_6), .kolizja_wiersz_7(main_4_kolizja_wiersz_7),
    .kolizja_wiersz_8(main_4_kolizja_wiersz_8), .kolizja_wiersz_9(main_4_kolizja_wiersz_9),
    .kolizja_wiersz_10(main_4_kolizja_wiersz_10), .kolizja_wiersz_11(main_4_kolizja_wiersz_11),
    .kolizja_wiersz_12(main_4_kolizja_wiersz_12), .kolizja_wiersz_13(main_4_kolizja_wiersz_13),
    .kolizja_wiersz_14(main_4_kolizja_wiersz_14), .kolizja_wiersz_15(main_4_kolizja_wiersz_15),
    .out_20(main_4_out_20), .out_21(main_4_out_21), .out_22(main_4_out_22), .out_23(main_4_out_23),
    .out_24(main_4_out_24), .out_25(main_4_out_25), .out_26(main_4_out_26), .out_27(main_4_out_27),
    .out_28(main_4_out_28), .out_29(main_4_out_29), .out_30(main_4_out_30), .out_31(main_4_out_31),
    .out_32(main_4_out_32), .out_33(main_4_out_33), .out_34(main_4_out_34), .out_35(main_4_out_35));
  DotMatrix #(.inputtype("row"), .matrixcols(32), .matrixrows(16)) dotmatrix_2 (
    .row0(main_4_out_20), .row1(main_4_out_21), .row2(main_4_out_22), .row3(main_4_out_23),
    .row4(main_4_out_24), .row5(main_4_out_25), .row6(main_4_out_26), .row7(main_4_out_27),
    .row8(main_4_out_28), .row9(main_4_out_29), .row10(main_4_out_30), .row11(main_4_out_31),
    .row12(main_4_out_32), .row13(main_4_out_33), .row14(main_4_out_34), .row15(main_4_out_35));
  Button \reset_lub_wciśnij_klawisz_r  (.out(\reset_lub_wciśnij_klawisz_r_out ));
  Comparator #(.width(7)) comparator_1 (.a(keyboard_1_data), .b(7'b0100000), .eq(comparator_1_eq));  // open: gt, lt
  Comparator #(.width(7)) comparator_2 (.a(keyboard_1_data), .b(7'b1110010), .eq(comparator_2_eq));  // open: gt, lt
  or or_1 (or_1_out, comparator_1_eq, \skok_lub_wciśnij_spacje_out );
  or or_2 (or_2_out, \reset_lub_wciśnij_klawisz_r_out , comparator_2_eq);
  Button \skok_lub_wciśnij_spacje  (.out(\skok_lub_wciśnij_spacje_out ));
  \wynik_wyświetlanie_duży_main  main_5 (
    .clock(_32_out), .stop(main_3_out_17), .out_4(main_5_out_4), .out_5(main_5_out_5), .out_6(main_5_out_6),
    .out_7(main_5_out_7), .out_8(main_5_out_8), .out_9(main_5_out_9), .out_10(main_5_out_10),
    .out_11(main_5_out_11), .out_12(main_5_out_12), .out_13(main_5_out_13), .out_14(main_5_out_14),
    .out_15(main_5_out_15), .out_16(main_5_out_16), .out_17(main_5_out_17), .out_18(main_5_out_18),
    .out_19(main_5_out_19), .out_20(main_5_out_20), .out_21(main_5_out_21), .out_22(main_5_out_22),
    .out_23(main_5_out_23), .out_24(main_5_out_24), .out_25(main_5_out_25), .out_26(main_5_out_26),
    .out_27(main_5_out_27), .out_28(main_5_out_28), .out_29(main_5_out_29), .out_30(main_5_out_30),
    .out_31(main_5_out_31), .out_32(main_5_out_32), .out_33(main_5_out_33), .out_34(main_5_out_34),
    .out_35(main_5_out_35), .reset(or_2_out), ._100(main_5__100), ._1000(main_5__1000), ._10000(main_5__10000));
endmodule
