// Logisim project przegrana.circ as structural Verilog: 1 circuit, main circuit main
module main (
  input  reset,
  input  [31:0] in_2,
  input  [31:0] in_3,
  input  [31:0] in_4,
  input  [31:0] in_5,
  input  [31:0] in_6,
  input  [31:0] in_7,
  input  [31:0] in_8,
  input  [31:0] in_9,
  input  [31:0] in_10,
  input  [31:0] in_11,
  input  [31:0] in_12,
  input  [31:0] in_13,
  input  [31:0] in_14,
  input  [31:0] in_15,
  input  [31:0] in_16,
  output out_17
);

  wire and_1_out, or_1_out, or_2_out, or_4_out, or_5_out, or_6_out, or_7_out, or_8_out, or_9_out, or_10_out,
       or_11_out, or_12_out, or_13_out, or_14_out, or_15_out, or_16_out, or_17_out;
  wire [2:0] counter_1_q;

  or or_1 (or_1_out, in_4[31], in_4[30], in_4[29], in_4[28], in_4[27], in_4[26], in_4[25], in_4[24], in_4[23], in_4[22], in_4[21], in_4[20], in_4[19], in_4[18], in_4[17], in_4[16], in_4[14], in_4[13], in_4[12], in_4[11], in_4[10], in_4[9], in_4[8], in_4[7], in_4[6], in_4[5], in_4[4], in_4[3], in_4[2], in_4[1], in_4[0], in_4[15]);
  or or_2 (or_2_out, in_5[31], in_5[30], in_5[29], in_5[28], in_5[27], in_5[26], in_5[25], in_5[24], in_5[23], in_5[22], in_5[21], in_5[20], in_5[19], in_5[18], in_5[17], in_5[16], in_5[14], in_5[13], in_5[12], in_5[11], in_5[10], in_5[9], in_5[8], in_5[7], in_5[6], in_5[5], in_5[4], in_5[3], in_5[2], in_5[1], in_5[0], in_5[15]);
  or or_3 (out_17, counter_1_q[2], counter_1_q[1], counter_1_q[0]);
  and and_1 (and_1_out, reset, out_17);
  Counter #(.width(3), .max('h7)) counter_1 (
    .Q(counter_1_q), .clk(or_5_out), .clr(and_1_out));  // open: load, D, count, carry
  or or_4 (or_4_out, in_6[31], in_6[30], in_6[29], in_6[28], in_6[27], in_6[26], in_6[25], in_6[24], in_6[23], in_6[22], in_6[21], in_6[20], in_6[19], in_6[18], in_6[17], in_6[16], in_6[14], in_6[13], in_6[12], in_6[11], in_6[10], in_6[9], in_6[8], in_6[7], in_6[6], in_6[5], in_6[4], in_6[3], in_6[2], in_6[1], in_6[0], in_6[15]);
  or or_5 (or_5_out, or_1_out, or_2_out, or_4_out, or_6_out, or_7_out, or_8_out, or_9_out, or_10_out, or_11_out, or_12_out, or_13_out, or_14_out, or_15_out, or_16_out, or_17_out);
  or or_6 (or_6_out, in_7[31], in_7[30], in_7[29], in_7[28], in_7[27], in_7[26], in_7[25], in_7[24], in_7[23], in_7[22], in_7[21], in_7[20], in_7[19], in_7[18], in_7[17], in_7[16], in_7[14], in_7[13], in_7[12], in_7[11], in_7[10], in_7[9], in_7[8], in_7[7], in_7[6], in_7[5], in_7[4], in_7[3], in_7[2], in_7[1], in_7[0], in_7[15]);
  or or_7 (or_7_out, in_8[31], in_8[30], in_8[29], in_8[28], in_8[27], in_8[26], in_8[25], in_8[24], in_8[23], in_8[22], in_8[21], in_8[20], in_8[19], in_8[18], in_8[17], in_8[16], in_8[14], in_8[13], in_8[12], in_8[11], in_8[10], in_8[9], in_8[8], in_8[7], in_8[6], in_8[5], in_8[4], in_8[3], in_8[2], in_8[1], in_8[0], in_8[15]);
  or or_8 (or_8_out, in_9[31], in_9[30], in_9[29], in_9[28], in_9[27], in_9[26], in_9[25], in_9[24], in_9[23], in_9[22], in_9[21], in_9[20], in_9[19], in_9[18], in_9[17], in_9[16], in_9[14], in_9[13], in_9[12], in_9[11], in_9[10], in_9[9], in_9[8], in_9[7], in_9[6], in_9[5], in_9[4], in_9[3], in_9[2], in_9[1], in_9[0], in_9[15]);
  or or_9 (or_9_out, in_10[31], in_10[30], in_10[29], in_10[28], in_10[27], in_10[26], in_10[25], in_10[24], in_10[23], in_10[22], in_10[21], in_10[20], in_10[19], in_10[18], in_10[17], in_10[16], in_10[14], in_10[13], in_10[12], in_10[11], in_10[10], in_10[9], in_10[8], in_10[7], in_10[6], in_10[5], in_10[4], in_10[3], in_10[2], in_10[1], in_10[0], in_10[15]);
  or or_10 (or_10_out, in_11[31], in_11[30], in_11[29], in_11[28], in_11[27], in_11[26], in_11[25], in_11[24], in_11[23], in_11[22], in_11[21], in_11[20], in_11[19], in_11[18], in_11[17], in_11[16], in_11[14], in_11[13], in_11[12], in_11[11], in_11[10], in_11[9], in_11[8], in_11[7], in_11[6], in_11[5], in_11[4], in_11[3], in_11[2], in_11[1], in_11[0], in_11[15]);
  or or_11 (or_11_out, in_12[31], in_12[30], in_12[29], in_12[28], in_12[27], in_12[26], in_12[25], in_12[24], in_12[23], in_12[22], in_12[21], in_12[20], in_12[19], in_12[18], in_12[17], in_12[16], in_12[14], in_12[13], in_12[12], in_12[11], in_12[10], in_12[9], in_12[8], in_12[7], in_12[6], in_12[5], in_12[4], in_12[3], in_12[2], in_12[1], in_12[0], in_12[15]);
  or or_12 (or_12_out, in_13[31], in_13[30], in_13[29], in_13[28], in_13[27], in_13[26], in_13[25], in_13[24], in_13[23], in_13[22], in_13[21], in_13[20], in_13[19], in_13[18], in_13[17], in_13[16], in_13[14], in_13[13], in_13[12], in_13[11], in_13[10], in_13[9], in_13[8], in_13[7], in_13[6], in_13[5], in_13[4], in_13[3], in_13[2], in_13[1], in_13[0], in_13[15]);
  or or_13 (or_13_out, in_14[31], in_14[30], in_14[29], in_14[28], in_14[27], in_14[26], in_14[25], in_14[24], in_14[23], in_14[22], in_14[21], in_14[20], in_14[19], in_14[18], in_14[17], in_14[16], in_14[14], in_14[13], in_14[12], in_14[11], in_14[10], in_14[9], in_14[8], in_14[7], in_14[6], in_14[5], in_14[4], in_14[3], in_14[2], in_14[1], in_14[0], in_14[15]);
  or or_14 (or_14_out, in_15[31], in_15[30], in_15[29], in_15[28], in_15[27], in_15[26], in_15[25], in_15[24], in_15[23], in_15[22], in_15[21], in_15[20], in_15[19], in_15[18], in_15[17], in_15[16], in_15[14], in_15[13], in_15[12], in_15[11], in_15[10], in_15[9], in_15[8], in_15[7], in_15[6], in_15[5], in_15[4], in_15[3], in_15[2], in_15[1], in_15[0], in_15[15]);
  or or_15 (or_15_out, in_16[31], in_16[30], in_16[29], in_16[28], in_16[27], in_16[26], in_16[25], in_16[24], in_16[23], in_16[22], in_16[21], in_16[20], in_16[19], in_16[18], in_16[17], in_16[16], in_16[14], in_16[13], in_16[12], in_16[11], in_16[10], in_16[9], in_16[8], in_16[7], in_16[6], in_16[5], in_16[4], in_16[3], in_16[2], in_16[1], in_16[0], in_16[15]);
  or or_16 (or_16_out, in_2[31], in_2[30], in_2[29], in_2[28], in_2[27], in_2[26], in_2[25], in_2[24], in_2[23], in_2[22], in_2[21], in_2[20], in_2[19], in_2[18], in_2[17], in_2[16], in_2[14], in_2[13], in_2[12], in_2[11], in_2[10], in_2[9], in_2[8], in_2[7], in_2[6], in_2[5], in_2[4], in_2[3], in_2[2], in_2[1], in_2[0], in_2[15]);
  or or_17 (or_17_out, in_3[31], in_3[30], in_3[29], in_3[28], in_3[27], in_3[26], in_3[25], in_3[24], in_3[23], in_3[22], in_3[21], in_3[20], in_3[19], in_3[18], in_3[17], in_3[16], in_3[14], in_3[13], in_3[12], in_3[11], in_3[10], in_3[9], in_3[8], in_3[7], in_3[6], in_3[5], in_3[4], in_3[3], in_3[2], in_3[1], in_3[0], in_3[15]);
endmodule
