// Logisim project ptaki.circ as structural Verilog: 1 circuit, main circuit main
module main (
  input  [31:0] dino_gora,
  input  [31:0] in_2,
  input  [31:0] in_3,
  input  [31:0] in_4,
  input  [31:0] dino_dol,
  input  clock,
  input  stop,
  input  ptak,
  input  clock_do_stopu,
  output [31:0] kolizja_1,
  output [31:0] kolizja_2,
  output [31:0] kolizja_3,
  output [31:0] kolizja_4,
  output [31:0] kolizja_5,
  output [31:0] gora,
  output [31:0] out_16,
  output [31:0] out_17,
  output [31:0] out_18,
  output [31:0] dol,
  output \łałanakła 
);

  wire and_1_out, counter_1_q, main_10_clock_out, not_1_out, not_2_out, not_3_out, not_4_out, not_5_out,
       not_6_out, not_7_out, not_8_out, not_9_out, not_10_out, not_11_out, or_1_out, or_2_out;
  wire [31:0] controlled_buffer_1_out, controlled_buffer_2_out, controlled_buffer_3_out,
       controlled_buffer_4_out, controlled_buffer_9_out, controlled_buffer_11_out, controlled_buffer_13_out,
       controlled_buffer_15_out, controlled_buffer_17_out, controlled_buffer_19_out, main_1_kaktus_out,
       main_2_kaktus_out, main_3_kaktus_out, main_4_kaktus_out, main_5_kaktus_out, main_6_kaktus_out,
       main_7_kaktus_out, main_8_kaktus_out, main_9_kaktus_out, main_10_kaktus_out;

  or or_1 (or_1_out, stop, ~ptak);  // OR_Gate
  and and_1 (and_1_out, clock, ptak);
  not not_1 (not_1_out, ptak);
  kaktus_wyswietlanie_main main_1 (
    .kaktus_0_klatka({32{1'b0}}), .kaktus_1_klatka({32{1'b0}}), .kaktus_2_klatka({32{1'b0}}),
    .kaktus_3_klatka({32{1'b0}}), .kaktus_4klatka({32{1'b0}}), .kaktus_5_klatka({32{1'b0}}),
    .clock(and_1_out), .stop(or_1_out), .kaktus_out(main_1_kaktus_out));  // open: clock_out
  kaktus_wyswietlanie_main main_2 (
    .kaktus_0_klatka({32{1'b0}}), .kaktus_1_klatka({32{1'b0}}), .kaktus_2_klatka({32{1'b0}}),
    .kaktus_3_klatka(32'h1), .kaktus_4klatka(32'h2), .kaktus_5_klatka(32'h4), .clock(and_1_out),
    .stop(or_1_out), .kaktus_out(main_2_kaktus_out));  // open: clock_out
  kaktus_wyswietlanie_main main_3 (
    .kaktus_0_klatka({32{1'b0}}), .kaktus_1_klatka(32'h3), .kaktus_2_klatka(32'h6), .kaktus_3_klatka(32'hc),
    .kaktus_4klatka(32'h18), .kaktus_5_klatka(32'h30), .clock(and_1_out), .stop(or_1_out),
    .kaktus_out(main_3_kaktus_out));  // open: clock_out
  kaktus_wyswietlanie_main main_4 (
    .kaktus_0_klatka({32{1'b0}}), .kaktus_1_klatka(32'h3), .kaktus_2_klatka(32'h7), .kaktus_3_klatka(32'hf),
    .kaktus_4klatka(32'h1f), .kaktus_5_klatka(32'h3e), .clock(and_1_out), .stop(or_1_out),
    .kaktus_out(main_4_kaktus_out));  // open: clock_out
  kaktus_wyswietlanie_main main_5 (
    .kaktus_0_klatka({32{1'b0}}), .kaktus_1_klatka(32'h1), .kaktus_2_klatka(32'h3), .kaktus_3_klatka(32'h7),
    .kaktus_4klatka(32'hf), .kaktus_5_klatka(32'h1f), .clock(and_1_out), .stop(or_1_out),
    .kaktus_out(main_5_kaktus_out));  // open: clock_out
  kaktus_wyswietlanie_main main_6 (
    .kaktus_0_klatka({32{1'b0}}), .kaktus_1_klatka(32'h1), .kaktus_2_klatka(32'h3), .kaktus_3_klatka(32'h7),
    .kaktus_4klatka(32'hf), .kaktus_5_klatka(32'h1f), .clock(and_1_out), .stop(or_1_out),
    .kaktus_out(main_6_kaktus_out));  // open: clock_out
  kaktus_wyswietlanie_main main_7 (
    .kaktus_0_klatka({32{1'b0}}), .kaktus_1_klatka({32{1'b0}}), .kaktus_2_klatka(32'h1),
    .kaktus_3_klatka(32'h3), .kaktus_4klatka(32'h7), .kaktus_5_klatka(32'he), .clock(and_1_out),
    .stop(or_1_out), .kaktus_out(main_7_kaktus_out));  // open: clock_out
  kaktus_wyswietlanie_main main_8 (
    .kaktus_0_klatka({32{1'b0}}), .kaktus_1_klatka({32{1'b0}}), .kaktus_2_klatka({32{1'b0}}),
    .kaktus_3_klatka({32{1'b0}}), .kaktus_4klatka({32{1'b0}}), .kaktus_5_klatka({32{1'b0}}),
    .clock(and_1_out), .stop(or_1_out), .kaktus_out(main_8_kaktus_out));  // open: clock_out
  kaktus_wyswietlanie_main main_9 (
    .kaktus_0_klatka({32{1'b0}}), .kaktus_1_klatka({32{1'b0}}), .kaktus_2_klatka({32{1'b0}}),
    .kaktus_3_klatka(32'h1), .kaktus_4klatka(32'h2), .kaktus_5_klatka(32'h4), .clock(and_1_out),
    .stop(or_1_out), .kaktus_out(main_9_kaktus_out));  // open: clock_out
  kaktus_wyswietlanie_main main_10 (
    .kaktus_0_klatka({32{1'b0}}), .kaktus_1_klatka({32{1'b0}}), .kaktus_2_klatka({32{1'b0}}),
    .kaktus_3_klatka({32{1'b0}}), .kaktus_4klatka({32{1'b0}}), .kaktus_5_klatka({32{1'b0}}),
    .clock(and_1_out), .stop(or_1_out), .kaktus_out(main_10_kaktus_out), .clock_out(main_10_clock_out));
  assign controlled_buffer_1_out = counter_1_q ? main_2_kaktus_out : 32'bz;  // Controlled_Buffer controlled_buffer_1
  assign controlled_buffer_2_out = counter_1_q ? main_4_kaktus_out : 32'bz;  // Controlled_Buffer controlled_buffer_2
  assign controlled_buffer_3_out = counter_1_q ? main_6_kaktus_out : 32'bz;  // Controlled_Buffer controlled_buffer_3
  assign controlled_buffer_4_out = counter_1_q ? main_8_kaktus_out : 32'bz;  // Controlled_Buffer controlled_buffer_4
  assign controlled_buffer_1_out = not_2_out ? main_1_kaktus_out : 32'bz;  // Controlled_Buffer controlled_buffer_5
  not not_2 (not_2_out, counter_1_q);
  assign controlled_buffer_2_out = not_3_out ? main_3_kaktus_out : 32'bz;  // Controlled_Buffer controlled_buffer_6
  not not_3 (not_3_out, counter_1_q);
  assign controlled_buffer_3_out = not_4_out ? main_5_kaktus_out : 32'bz;  // Controlled_Buffer controlled_buffer_7
  not not_4 (not_4_out, counter_1_q);
  assign controlled_buffer_4_out = not_5_out ? main_7_kaktus_out : 32'bz;  // Controlled_Buffer controlled_buffer_8
  not not_5 (not_5_out, counter_1_q);
  assign controlled_buffer_9_out = not_6_out ? main_9_kaktus_out : 32'bz;  // Controlled_Buffer controlled_buffer_9
  not not_6 (not_6_out, counter_1_q);
  assign controlled_buffer_9_out = counter_1_q ? main_10_kaktus_out : 32'bz;  // Controlled_Buffer controlled_buffer_10
  Counter #(.width(1), .max('h1)) counter_1 (.Q(counter_1_q), .clk(and_1_out));  // open: load, D, count, carry, clr
  not not_7 (not_7_out, or_2_out);
  assign controlled_buffer_11_out = or_2_out ? {32{1'b0}} : 32'bz;  // Controlled_Buffer controlled_buffer_11
  assign controlled_buffer_11_out = not_8_out ? controlled_buffer_2_out : 32'bz;  // Controlled_Buffer controlled_buffer_12
  not not_8 (not_8_out, or_2_out);
  assign controlled_buffer_13_out = or_2_out ? {32{1'b0}} : 32'bz;  // Controlled_Buffer controlled_buffer_13
  assign controlled_buffer_13_out = not_9_out ? controlled_buffer_3_out : 32'bz;  // Controlled_Buffer controlled_buffer_14
  not not_9 (not_9_out, or_2_out);
  assign controlled_buffer_15_out = or_2_out ? {32{1'b0}} : 32'bz;  // Controlled_Buffer controlled_buffer_15
  assign controlled_buffer_15_out = not_10_out ? controlled_buffer_4_out : 32'bz;  // Controlled_Buffer controlled_buffer_16
  not not_10 (not_10_out, or_2_out);
  assign controlled_buffer_17_out = or_2_out ? {32{1'b0}} : 32'bz;  // Controlled_Buffer controlled_buffer_17
  assign controlled_buffer_17_out = not_11_out ? controlled_buffer_9_out : 32'bz;  // Controlled_Buffer controlled_buffer_18
  not not_11 (not_11_out, or_2_out);
  or or_2 (or_2_out, or_1_out, not_1_out);
  assign controlled_buffer_19_out = or_2_out ? {32{1'b0}} : 32'bz;  // Controlled_Buffer controlled_buffer_19
  assign controlled_buffer_19_out = not_7_out ? controlled_buffer_1_out : 32'bz;  // Controlled_Buffer controlled_buffer_20
  and and_2 (\łałanakła , main_10_clock_out, ~not_1_out);  // AND_Gate
  probaled2_main main_11 (
    .dinozaur(dino_gora), .kaktus(controlled_buffer_19_out), .clock(\łałanakła ),
    .clock_do_stopu(clock_do_stopu), .stop(or_1_out), .kolizja(kolizja_1), .obraz(gora));
  probaled2_main main_12 (
    .dinozaur(in_2), .kaktus(controlled_buffer_11_out), .clock(\łałanakła ), .clock_do_stopu(clock_do_stopu),
    .stop(or_1_out), .kolizja(kolizja_2), .obraz(out_16));
  probaled2_main main_13 (
    .dinozaur(in_3), .kaktus(controlled_buffer_13_out), .clock(\łałanakła ), .clock_do_stopu(clock_do_stopu),
    .stop(or_1_out), .kolizja(kolizja_3), .obraz(out_17));
  probaled2_main main_14 (
    .dinozaur(in_4), .kaktus(controlled_buffer_15_out), .clock(\łałanakła ), .clock_do_stopu(clock_do_stopu),
    .stop(or_1_out), .kolizja(kolizja_4), .obraz(out_18));
  probaled2_main main_15 (
    .dinozaur(dino_dol), .kaktus(controlled_buffer_17_out), .clock(\łałanakła ),
    .clock_do_stopu(clock_do_stopu), .stop(or_1_out), .kolizja(kolizja_5), .obraz(dol));
endmodule
