// Logisim project wynik wyświetlanie duży.circ as structural Verilog: 1 circuit, main circuit main
module main (
  input  reset,
  input  clock,
  input  stop,
  output [15:0] out_4,
  output [15:0] out_5,
  output [15:0] out_6,
  output [15:0] out_7,
  output [15:0] out_8,
  output [15:0] out_9,
  output [15:0] out_10,
  output [15:0] out_11,
  output [15:0] out_12,
  output [15:0] out_13,
  output [15:0] out_14,
  output [15:0] out_15,
  output [15:0] out_16,
  output [15:0] out_17,
  output [15:0] out_18,
  output [15:0] out_19,
  output [15:0] out_20,
  output [15:0] out_21,
  output [15:0] out_22,
  output [15:0] out_23,
  output [15:0] out_24,
  output [15:0] out_25,
  output [15:0] out_26,
  output [15:0] out_27,
  output [15:0] out_28,
  output [15:0] out_29,
  output [15:0] out_30,
  output [15:0] out_31,
  output [15:0] out_32,
  output [15:0] out_33,
  output [15:0] out_34,
  output [15:0] out_35,
  output _100,
  output _1000,
  output _10000
);

  wire and_1_out, counter_1_q, counter_3_q, main_2__10, main_3__10, main_4__10, main_5__10, main_6__10,
       main_7__10, main_8__10, or_1_out, or_2_out, or_3_out;

  and and_1 (and_1_out, clock, ~stop);  // AND_Gate
  \wynik_wyświetlanie_mały_main  main_1 (
    .out_3(out_4), .out_4(out_5), .out_5(out_6), .clock(main_2__10), .reset(reset));  // open: _10
  \wynik_wyświetlanie_mały_main  main_2 (
    ._10(main_2__10), .out_3(out_8), .out_4(out_9), .out_5(out_10), .clock(main_3__10), .reset(reset));
  \wynik_wyświetlanie_mały_main  main_3 (
    ._10(main_3__10), .out_3(out_12), .out_4(out_13), .out_5(out_14), .clock(main_4__10), .reset(reset));
  \wynik_wyświetlanie_mały_main  main_4 (
    ._10(main_4__10), .out_3(out_16), .out_4(out_17), .out_5(out_18), .clock(main_5__10), .reset(reset));
  \wynik_wyświetlanie_mały_main  main_5 (
    ._10(main_5__10), .out_3(out_20), .out_4(out_21), .out_5(out_22), .clock(main_6__10), .reset(reset));
  \wynik_wyświetlanie_mały_main  main_6 (
    ._10(main_6__10), .out_3(out_24), .out_4(out_25), .out_5(out_26), .clock(main_7__10), .reset(reset));
  or or_1 (or_1_out, stop, reset);
  Counter #(.width(1), .max('h1), .ongoal("stay")) counter_1 (
    .Q(counter_1_q), .clk(main_6__10), .clr(or_2_out));  // open: load, D, count, carry
  or or_2 (or_2_out, main_5__10, or_1_out);
  Counter #(.width(1), .max('h1), .ongoal("stay")) counter_2 (
    .Q(_10000), .clk(main_5__10), .clr(or_1_out));  // open: load, D, count, carry
  Counter #(.width(1), .max('h1), .ongoal("stay")) counter_3 (
    .Q(counter_3_q), .clk(main_7__10), .clr(or_3_out));  // open: load, D, count, carry
  or or_3 (or_3_out, main_6__10, or_1_out);
  and and_2 (_100, counter_3_q, ~counter_1_q);  // AND_Gate
  and and_3 (_1000, counter_1_q, ~_10000);  // AND_Gate
  \wynik_wyświetlanie_mały_main  main_7 (
    ._10(main_7__10), .out_3(out_28), .out_4(out_29), .out_5(out_30), .clock(main_8__10), .reset(reset));
  \wynik_wyświetlanie_mały_main  main_8 (
    ._10(main_8__10), .out_3(out_32), .out_4(out_33), .out_5(out_34), .clock(and_1_out), .reset(reset));

  assign out_7 = {16{1'b0}};
  assign out_11 = {16{1'b0}};
  assign out_15 = {16{1'b0}};
  assign out_19 = {16{1'b0}};
  assign out_23 = {16{1'b0}};
  assign out_27 = {16{1'b0}};
  assign out_31 = {16{1'b0}};
  assign out_35 = {16{1'b0}};
endmodule
