// Logisim project wynik wyświetlanie mały.circ as structural Verilog: 1 circuit, main circuit main
module main (
  input  clock,
  input  reset,
  output [15:0] out_3,
  output [15:0] out_4,
  output [15:0] out_5,
  output _10
);

  wire and_1_out, and_2_out, and_3_out, and_4_out, and_5_out, and_6_out, and_7_out, and_8_out, and_9_out,
       and_11_out, or_1_out;
  wire [3:0] counter_1_q;

  and and_1 (and_1_out, ~counter_1_q[3], ~counter_1_q[2], ~counter_1_q[1], ~counter_1_q[0]);  // AND_Gate
  and and_2 (and_2_out, ~counter_1_q[3], ~counter_1_q[2], ~counter_1_q[1], counter_1_q[0]);  // AND_Gate
  and and_3 (and_3_out, ~counter_1_q[3], ~counter_1_q[2], counter_1_q[1], ~counter_1_q[0]);  // AND_Gate
  and and_4 (and_4_out, ~counter_1_q[3], ~counter_1_q[2], counter_1_q[1], counter_1_q[0]);  // AND_Gate
  Counter #(.width(4), .max('hf)) counter_1 (
    .Q(counter_1_q), .clk(clock), .clr(or_1_out));  // open: load, D, count, carry
  and and_5 (and_5_out, ~counter_1_q[3], counter_1_q[2], ~counter_1_q[1], ~counter_1_q[0]);  // AND_Gate
  and and_6 (and_6_out, ~counter_1_q[3], counter_1_q[2], counter_1_q[1], ~counter_1_q[0]);  // AND_Gate
  and and_7 (and_7_out, ~counter_1_q[3], counter_1_q[2], ~counter_1_q[1], counter_1_q[0]);  // AND_Gate
  or or_1 (or_1_out, _10, reset);
  and and_8 (and_8_out, ~counter_1_q[3], counter_1_q[2], counter_1_q[1], counter_1_q[0]);  // AND_Gate
  and and_9 (and_9_out, counter_1_q[3], ~counter_1_q[2], ~counter_1_q[1], ~counter_1_q[0]);  // AND_Gate
  and and_10 (_10, counter_1_q[3], ~counter_1_q[2], counter_1_q[1], ~counter_1_q[0]);  // AND_Gate
  and and_11 (and_11_out, counter_1_q[3], ~counter_1_q[2], ~counter_1_q[1], counter_1_q[0]);  // AND_Gate
  assign out_4 = and_1_out ? 16'h110 : 16'bz;  // Controlled_Buffer controlled_buffer_1
  assign out_5 = and_5_out ? 16'h1f0 : 16'bz;  // Controlled_Buffer controlled_buffer_2
  assign out_4 = and_5_out ? 16'h40 : 16'bz;  // Controlled_Buffer controlled_buffer_3
  assign out_3 = and_5_out ? 16'h1c0 : 16'bz;  // Controlled_Buffer controlled_buffer_4
  assign out_5 = and_7_out ? 16'h170 : 16'bz;  // Controlled_Buffer controlled_buffer_5
  assign out_4 = and_7_out ? 16'h150 : 16'bz;  // Controlled_Buffer controlled_buffer_6
  assign out_3 = and_7_out ? 16'h1d0 : 16'bz;  // Controlled_Buffer controlled_buffer_7
  assign out_5 = and_6_out ? 16'h170 : 16'bz;  // Controlled_Buffer controlled_buffer_8
  assign out_4 = and_6_out ? 16'h150 : 16'bz;  // Controlled_Buffer controlled_buffer_9
  assign out_3 = and_6_out ? 16'h1f0 : 16'bz;  // Controlled_Buffer controlled_buffer_10
  assign out_3 = and_8_out ? 16'h100 : 16'bz;  // Controlled_Buffer controlled_buffer_11
  assign out_4 = and_8_out ? 16'h100 : 16'bz;  // Controlled_Buffer controlled_buffer_12
  assign out_5 = and_8_out ? 16'h1f0 : 16'bz;  // Controlled_Buffer controlled_buffer_13
  assign out_5 = and_9_out ? 16'h1f0 : 16'bz;  // Controlled_Buffer controlled_buffer_14
  assign out_4 = and_9_out ? 16'h150 : 16'bz;  // Controlled_Buffer controlled_buffer_15
  assign out_3 = and_9_out ? 16'h1f0 : 16'bz;  // Controlled_Buffer controlled_buffer_16
  assign out_5 = and_11_out ? 16'h1f0 : 16'bz;  // Controlled_Buffer controlled_buffer_17
  assign out_4 = and_11_out ? 16'h150 : 16'bz;  // Controlled_Buffer controlled_buffer_18
  assign out_3 = and_11_out ? 16'h1d0 : 16'bz;  // Controlled_Buffer controlled_buffer_19
  assign out_5 = and_4_out ? 16'h1f0 : 16'bz;  // Controlled_Buffer controlled_buffer_20
  assign out_4 = and_4_out ? 16'h150 : 16'bz;  // Controlled_Buffer controlled_buffer_21
  assign out_3 = and_4_out ? 16'h150 : 16'bz;  // Controlled_Buffer controlled_buffer_22
  assign out_3 = and_3_out ? 16'h170 : 16'bz;  // Controlled_Buffer controlled_buffer_23
  assign out_4 = and_3_out ? 16'h150 : 16'bz;  // Controlled_Buffer controlled_buffer_24
  assign out_5 = and_3_out ? 16'h1d0 : 16'bz;  // Controlled_Buffer controlled_buffer_25
  assign out_5 = and_1_out ? 16'h1f0 : 16'bz;  // Controlled_Buffer controlled_buffer_26
  assign out_3 = and_1_out ? 16'h1f0 : 16'bz;  // Controlled_Buffer controlled_buffer_27
  assign out_4 = and_2_out ? {16{1'b0}} : 16'bz;  // Controlled_Buffer controlled_buffer_28
  assign out_3 = and_2_out ? {16{1'b0}} : 16'bz;  // Controlled_Buffer controlled_buffer_29
  assign out_5 = and_2_out ? 16'h1f0 : 16'bz;  // Controlled_Buffer controlled_buffer_30

  // Notes on the sheet:
  //   lewo
  //   prawo
  //   środek
  //   2
  //   4
  //   5
  //   6
  //   8
  //   3
  //   0
  //   środek
  //   kreska góra środek do 4
  //   7
  //   9
  //   1
  //   góra
  //   góra środek dol
  //   góra dół
  //   kreska
  //   kreska dół środek
  //   kreska góra środek
endmodule
